# Fritzing sketch CS207 P (saved by Fritzing 0.9.3b)

parts:
  Arduino_Uno = Arduino Uno (Rev3)
  Specker = Piezo Speaker
  1_621_RPM_HD_Premium_Planetary_Gear_Motor = DC Motor
  1_621_RPM_HD_Premium_Planetary_Gear_Motor_2 = DC Motor
  DFRobot_IR_Remote_Kit_for_Arduino = DFRobot IR Remote Kit [part_number=RB-Dfr-92]
  Assembled_Actobotics®_Dual_Motor_Controller = Dual Motor Controller
  Matrix_12V_3000mAh_NiMH_Battery = Matrix 12V 3000mAh NiMH Battery
  VCC1 = Battery

nets:
  N1: Arduino_Uno.D8, DFRobot_IR_Remote_Kit_for_Arduino.S
  N2: Arduino_Uno.D10_PWM/SS, Specker.pin1
  GND: Arduino_Uno.GND, DFRobot_IR_Remote_Kit_for_Arduino.GND, VCC1.-
  N3: Arduino_Uno.D6_PWM, Assembled_Actobotics®_Dual_Motor_Controller.PWM_Signal_2#132
  N4: Arduino_Uno.D7, Assembled_Actobotics®_Dual_Motor_Controller.PWM_Signal_2#141
  5V: Arduino_Uno.5V, Specker.pin2, DFRobot_IR_Remote_Kit_for_Arduino.VCC
  N5: Arduino_Uno.VIN, VCC1.+
  N6: 1_621_RPM_HD_Premium_Planetary_Gear_Motor.pin_1, Assembled_Actobotics®_Dual_Motor_Controller.Motor_2B
  N7: 1_621_RPM_HD_Premium_Planetary_Gear_Motor.pin_2, Assembled_Actobotics®_Dual_Motor_Controller.Motor_1A
  N8: 1_621_RPM_HD_Premium_Planetary_Gear_Motor_2.pin_1, Assembled_Actobotics®_Dual_Motor_Controller.Motor_1B
  N9: 1_621_RPM_HD_Premium_Planetary_Gear_Motor_2.pin_2, Assembled_Actobotics®_Dual_Motor_Controller.Motor_2A
  N10: Assembled_Actobotics®_Dual_Motor_Controller.+5V_(IN), Matrix_12V_3000mAh_NiMH_Battery.+
  N11: Assembled_Actobotics®_Dual_Motor_Controller.GND, Matrix_12V_3000mAh_NiMH_Battery.-

custom parts:
  DFRobot IR Remote Kit: 1.Provides a remote control capability to your project 2.Contains IR Remote Controller, IR Receiver Module and Digital Cable
  Dual Motor Controller: The Actobotics® Dual Motor Controller provides a compact solution for controlling 2 brushed DC motors. The small footprint of the controller fits down inside the channel and the mounting holes perfectly align with the hub pattern which perforates the Actobotics® building system. This controller has 4 selectable modes.
  Matrix 12V 3000mAh NiMH Battery: This Matrix brand 12V, 3000ma battery (OEM p/n 14-0014) is listed in the FTC 2016-2017 Game Manual Part 1 <RE03> as one of three approved batteries for the 2016-2017 season. It has a Tamiya connector and a in-line 20A fuse of the same style as the Power Distribution Module.
